// Logisim project PRO1.circ as structural Verilog: 3 circuits, main circuit main
module main (
  input  A,
  input  B,
  input  A_2,
  input  in_4,
  output OUTPUT
);

  wire and_1_out, and_2_out, and_3_out, not_1_out, not_2_out, or_1_out;

  not not_1 (not_1_out, A_2);
  not not_2 (not_2_out, in_4);
  and and_1 (and_1_out, A, B);
  and and_2 (and_2_out, not_1_out, in_4);
  and and_3 (and_3_out, A_2, not_2_out);
  not not_3 (OUTPUT, and_1_out);
  or or_1 (or_1_out, and_2_out, and_3_out);
  LED led_1 (.in(or_1_out));
endmodule

module _1BitFA (
  input  Cin,
  input  A,
  input  B,
  output out_4,
  output out_5
);

  wire C1_out, C2_out, C3_out, C4_out, C5_out, C6_out, C7_out, not_1_out, not_2_out, not_3_out;

  not not_1 (not_1_out, A);
  not not_2 (not_2_out, B);
  not not_3 (not_3_out, Cin);
  and C1 (C1_out, not_1_out, not_2_out, Cin);
  and C2 (C2_out, not_1_out, B, not_3_out);
  and C3 (C3_out, A, not_2_out, not_3_out);
  and C4 (C4_out, A, B, Cin);
  and C5 (C5_out, Cin, B);
  and C6 (C6_out, A, Cin);
  and C7 (C7_out, A, B);
  or SUM (out_4, C1_out, C2_out, C3_out, C4_out);
  or u_Cin (out_5, C5_out, C6_out, C7_out);
endmodule

module _8bitFullAdder (
  input  Cin,
  input  A1,
  input  A2,
  input  B1,
  input  B2,
  input  C1,
  input  C2,
  input  D1,
  input  D2,
  input  E1,
  input  E2,
  input  F1,
  input  F2,
  input  G1,
  input  G2,
  input  H1,
  input  H2
);

  wire n1bitfa_1_out_4, n1bitfa_1_out_5, n1bitfa_2_out_4, n1bitfa_2_out_5, n1bitfa_3_out_4, n1bitfa_3_out_5,
       n1bitfa_4_out_4, n1bitfa_4_out_5, n1bitfa_5_out_4, n1bitfa_5_out_5, n1bitfa_6_out_4, n1bitfa_6_out_5,
       n1bitfa_7_out_4, n1bitfa_7_out_5, n1bitfa_8_out_4, n1bitfa_8_out_5;

  _1BitFA u_1bitfa_1 (.A(A1), .B(A2), .Cin(Cin), .out_5(n1bitfa_1_out_5), .out_4(n1bitfa_1_out_4));
  _1BitFA u_1bitfa_2 (.A(B1), .B(B2), .Cin(n1bitfa_1_out_5), .out_5(n1bitfa_2_out_5), .out_4(n1bitfa_2_out_4));
  _1BitFA u_1bitfa_3 (.A(C1), .B(C2), .Cin(n1bitfa_2_out_5), .out_5(n1bitfa_3_out_5), .out_4(n1bitfa_3_out_4));
  _1BitFA u_1bitfa_4 (.A(D1), .B(D2), .Cin(n1bitfa_3_out_5), .out_5(n1bitfa_4_out_5), .out_4(n1bitfa_4_out_4));
  _1BitFA u_1bitfa_5 (.A(E1), .B(E2), .Cin(n1bitfa_4_out_5), .out_5(n1bitfa_5_out_5), .out_4(n1bitfa_5_out_4));
  _1BitFA u_1bitfa_6 (.A(F1), .B(F2), .Cin(n1bitfa_5_out_5), .out_5(n1bitfa_6_out_5), .out_4(n1bitfa_6_out_4));
  _1BitFA u_1bitfa_7 (.A(G1), .B(G2), .Cin(n1bitfa_6_out_5), .out_5(n1bitfa_7_out_5), .out_4(n1bitfa_7_out_4));
  _1BitFA u_1bitfa_8 (.A(H1), .B(H2), .Cin(n1bitfa_7_out_5), .out_5(n1bitfa_8_out_5), .out_4(n1bitfa_8_out_4));
  LED led_1 (.in(n1bitfa_8_out_5));
  LED O1 (.in(n1bitfa_1_out_4));
  LED O2 (.in(n1bitfa_2_out_4));
  LED O3 (.in(n1bitfa_3_out_4));
  LED O4 (.in(n1bitfa_4_out_4));
  LED O5 (.in(n1bitfa_5_out_4));
  LED O6 (.in(n1bitfa_6_out_4));
  LED O7 (.in(n1bitfa_7_out_4));
  LED O8 (.in(n1bitfa_8_out_4));
endmodule
